# Fritzing sketch GG Kart Testing Pins - long (saved by Fritzing 0.9.3b)
circuit board: 6.03063cm x 13.9683cm
breadboards: 1

parts:
  TV = Pad [width=1.8 height=4 connect=center]  # not connected
  TVL = Pad [width=1.8 height=4 connect=center]  # not connected
  G = Pad [width=1.8 height=4 connect=center]  # not connected
  RST = Pad [width=1.8 height=4 connect=center]  # not connected
  5V = Pad [width=1.8 height=4 connect=center]  # not connected
  A14 = Pad [width=1.8 height=4 connect=center]  # not connected
  IOR = Pad [width=1.8 height=4 connect=center]  # not connected
  A8 = Pad [width=1.8 height=4 connect=center]  # not connected
  G_2 = Pad [width=1.8 height=4 connect=center]  # not connected
  D5 = Pad [width=1.8 height=4 connect=center]  # not connected
  D2 = Pad [width=1.8 height=4 connect=center]  # not connected
  MO-7 = Pad [width=1.8 height=4 connect=center]  # not connected
  A10 = Pad [width=1.8 height=4 connect=center]  # not connected
  A11 = Pad [width=1.8 height=4 connect=center]  # not connected
  D7 = Pad [width=1.8 height=4 connect=center]  # not connected
  D3 = Pad [width=1.8 height=4 connect=center]  # not connected
  A7 = Pad [width=1.8 height=4 connect=center]  # not connected
  WR = Pad [width=1.8 height=4 connect=center]  # not connected
  34V = Pad [width=1.8 height=4 connect=center]  # not connected
  D0 = Pad [width=1.8 height=4 connect=center]  # not connected
  A1 = Pad [width=1.8 height=4 connect=center]  # not connected
  A3 = Pad [width=1.8 height=4 connect=center]  # not connected
  A5 = Pad [width=1.8 height=4 connect=center]  # not connected
  A13 = Pad [width=1.8 height=4 connect=center]
  G_3 = Pad [width=1.8 height=4 connect=center]
  D6 = Pad [width=1.8 height=4 connect=center]
  D1 = Pad [width=1.8 height=4 connect=center]
  A12 = Pad [width=1.8 height=4 connect=center]
  M8-B = Pad [width=1.8 height=4 connect=center]
  A4 = Pad [width=1.8 height=4 connect=center]
  CLK = Pad [width=1.8 height=4 connect=center]
  5V_2 = Pad [width=1.8 height=4 connect=center]
  Refr = Pad [width=1.8 height=4 connect=center]
  A0 = Pad [width=1.8 height=4 connect=center]
  A15 = Pad [width=1.8 height=4 connect=center]
  Rd = Pad [width=1.8 height=4 connect=center]
  D4 = Pad [width=1.8 height=4 connect=center]
  M1 = Pad [width=1.8 height=4 connect=center]
  GG = Pad [width=1.8 height=4 connect=center]
  CE = Pad [width=1.8 height=4 connect=center]
  A2 = Pad [width=1.8 height=4 connect=center]
  G_4 = Pad [width=1.8 height=4 connect=center]
  TVR = Pad [width=1.8 height=4 connect=center]
  A6 = Pad [width=1.8 height=4 connect=center]
  A9 = Pad [width=1.8 height=4 connect=center]
  Pad1 = Pad [width=0.28222222222222221 height=0.28222222222222221 connect=center]
  Pad2 = Pad [width=0.28222222222222221 height=0.28222222222222221 connect=center]
  Pad3 = Pad [width=0.28222222222222221 height=0.28222222222222221 connect=center]
  Pad4 = Pad [width=0.28222222222222221 height=0.28222222222222221 connect=center]
  Pad5 = Pad [width=0.28222222222222221 height=0.28222222222222221 connect=center]
  Pad6 = Pad [width=0.28222222222222221 height=0.28222222222222221 connect=center]
  Pad7 = Pad [width=0.28222222222222221 height=0.28222222222222221 connect=center]
  Pad8 = Pad [width=0.28222222222222221 height=0.28222222222222221 connect=center]
  Pad9 = Pad [width=0.28222222222222221 height=0.28222222222222221 connect=center]
  Pad10 = Pad [width=0.28222222222222221 height=0.28222222222222221 connect=center]  # not connected
  Pad11 = Pad [width=0.28222222222222221 height=0.28222222222222221 connect=center]
  Pad12 = Pad [width=0.28222222222222221 height=0.28222222222222221 connect=center]
  Pad13 = Pad [width=0.28222222222222221 height=0.28222222222222221 connect=center]  # not connected
  Pad14 = Pad [width=0.28222222222222221 height=0.28222222222222221 connect=center]  # not connected
  Pad15 = Pad [width=0.28222222222222221 height=0.28222222222222221 connect=center]  # not connected
  Pad16 = Pad [width=0.28222222222222221 height=0.28222222222222221 connect=center]  # not connected
  Pad17 = Pad [width=0.28222222222222221 height=0.28222222222222221 connect=center]  # not connected
  Pad18 = Pad [width=0.28222222222222221 height=0.28222222222222221 connect=center]  # not connected
  Pad19 = Pad [width=0.28222222222222221 height=0.28222222222222221 connect=center]  # not connected
  Pad20 = Pad [width=0.28222222222222221 height=0.28222222222222221 connect=center]  # not connected
  Pad21 = Pad [width=0.28222222222222221 height=0.28222222222222221 connect=center]  # not connected
  Pad22 = Pad [width=0.28222222222222221 height=0.28222222222222221 connect=center]  # not connected
  Pad23 = Pad [width=0.28222222222222221 height=0.28222222222222221 connect=center]  # not connected
  Pad24 = Pad [width=0.28222222222222221 height=0.28222222222222221 connect=center]  # not connected
  Pad25 = Pad [width=0.28222222222222221 height=0.28222222222222221 connect=center]
  Pad26 = Pad [width=0.28222222222222221 height=0.28222222222222221 connect=center]  # not connected
  Pad27 = Pad [width=0.28222222222222221 height=0.28222222222222221 connect=center]
  Pad28 = Pad [width=0.28222222222222221 height=0.28222222222222221 connect=center]  # not connected
  Pad29 = Pad [width=0.28222222222222221 height=0.28222222222222221 connect=center]
  Pad30 = Pad [width=0.28222222222222221 height=0.28222222222222221 connect=center]  # not connected
  Pad31 = Pad [width=0.28222222222222221 height=0.28222222222222221 connect=center]
  Pad32 = Pad [width=0.28222222222222221 height=0.28222222222222221 connect=center]
  Pad33 = Pad [width=0.28222222222222221 height=0.28222222222222221 connect=center]  # not connected
  Pad34 = Pad [width=0.28222222222222221 height=0.28222222222222221 connect=center]
  Pad35 = Pad [width=0.28222222222222221 height=0.28222222222222221 connect=center]  # not connected
  Pad36 = Pad [width=0.28222222222222221 height=0.28222222222222221 connect=center]  # not connected
  Pad37 = Pad [width=0.28222222222222221 height=0.28222222222222221 connect=center]  # not connected
  Pad38 = Pad [width=0.28222222222222221 height=0.28222222222222221 connect=center]
  Pad39 = Pad [width=0.28222222222222221 height=0.28222222222222221 connect=center]  # not connected
  Pad40 = Pad [width=0.28222222222222221 height=0.28222222222222221 connect=center]
  Pad41 = Pad [width=0.28222222222222221 height=0.28222222222222221 connect=center]  # not connected
  Pad42 = Pad [width=0.28222222222222221 height=0.28222222222222221 connect=center]  # not connected
  Pad43 = Pad [width=0.28222222222222221 height=0.28222222222222221 connect=center]
  Pad44 = Pad [width=0.28222222222222221 height=0.28222222222222221 connect=center]
  Pad45 = Pad [width=0.28222222222222221 height=0.28222222222222221 connect=center]
  Pad46 = Pad [width=0.28222222222222221 height=0.28222222222222221 connect=center]  # not connected
  Pad47 = Pad [width=0.28222222222222221 height=0.28222222222222221 connect=center]  # not connected
  Pad48 = Pad [width=0.28222222222222221 height=0.28222222222222221 connect=center]  # not connected
  Pad49 = Pad [width=0.28222222222222221 height=0.28222222222222221 connect=center]  # not connected
  Pad50 = Pad [width=1.7916372540489107 height=0.98511085576570412 connect=center]  # not connected
  Pad51 = Pad [width=1.7916372540489107 height=0.98511085576570412 connect=center]  # not connected
  Pad52 = Pad [width=1.7916372540489107 height=0.98511085576570412 connect=center]  # not connected
  Pad53 = Pad [width=1.7916372540489107 height=0.98511085576570412 connect=center]  # not connected
  Pad54 = Pad [width=1.7916372540489107 height=0.98511085576570412 connect=center]  # not connected
  Pad55 = Pad [width=1.7916372540489107 height=0.98511085576570412 connect=center]  # not connected
  Pad56 = Pad [width=1.7916372540489107 height=0.98511085576570412 connect=center]  # not connected
  Pad57 = Pad [width=1.7916372540489107 height=0.98511085576570412 connect=center]  # not connected
  Pad58 = Pad [width=1.7916372540489107 height=0.98511085576570412 connect=center]  # not connected
  Pad59 = Pad [width=1.7916372540489107 height=0.98511085576570412 connect=center]  # not connected
  Pad60 = Pad [width=1.7916372540489107 height=0.98511085576570412 connect=center]  # not connected
  Pad61 = Pad [width=1.7916372540489107 height=0.98511085576570412 connect=center]  # not connected
  Pad62 = Pad [width=1.7916372540489107 height=0.98511085576570412 connect=center]  # not connected
  Pad63 = Pad [width=1.7916372540489107 height=0.98511085576570412 connect=center]  # not connected
  Pad64 = Pad [width=1.7916372540489107 height=0.98511085576570412 connect=center]  # not connected
  Pad65 = Pad [width=1.7916372540489107 height=0.98511085576570412 connect=center]  # not connected
  Pad66 = Pad [width=1.7916372540489107 height=0.98511085576570412 connect=center]  # not connected
  Pad67 = Pad [width=1.7916372540489107 height=0.98511085576570412 connect=center]  # not connected
  Pad68 = Pad [width=1.7916372540489107 height=0.98511085576570412 connect=center]  # not connected
  Pad69 = Pad [width=1.7916372540489107 height=0.98511085576570412 connect=center]  # not connected
  Pad70 = Pad [width=1.7916372540489107 height=0.98511085576570412 connect=center]  # not connected
  Pad71 = Pad [width=1.7916372540489107 height=0.98511085576570412 connect=center]  # not connected
  Pad72 = Pad [width=1.7916372540489107 height=0.98511085576570412 connect=center]  # not connected
  Pad73 = Pad [width=1.7916372540489107 height=0.98511085576570412 connect=center]  # not connected
  Pad74 = Pad [width=1.7916372540489107 height=0.98511085576570412 connect=center]  # not connected
  Pad75 = Pad [width=1.7916372540489107 height=0.98511085576570412 connect=center]  # not connected
  Pad76 = Pad [width=1.7916372540489107 height=0.98511085576570412 connect=center]  # not connected
  Pad77 = Pad [width=1.7916372540489107 height=0.98511085576570412 connect=center]  # not connected
  Pad78 = Pad [width=1.7916372540489107 height=0.98511085576570412 connect=center]  # not connected
  Pad79 = Pad [width=1.7916372540489107 height=0.98511085576570412 connect=center]  # not connected
  Pad80 = Pad [width=1.7916372540489107 height=0.98511085576570412 connect=center]  # not connected
  Pad81 = Pad [width=1.7916372540489107 height=0.98511085576570412 connect=center]  # not connected
  Pad82 = Pad [width=1.7916372540489107 height=0.98511085576570412 connect=center]  # not connected
  Pad83 = Pad [width=1.7916372540489107 height=0.98511085576570412 connect=center]  # not connected
  Pad84 = Pad [width=1.7916372540489107 height=0.98511085576570412 connect=center]  # not connected
  Pad85 = Pad [width=1.7916372540489107 height=0.98511085576570412 connect=center]  # not connected
  Pad86 = Pad [width=1.7916372540489107 height=0.98511085576570412 connect=center]  # not connected
  Pad87 = Pad [width=1.7916372540489107 height=0.98511085576570412 connect=center]  # not connected
  Pad88 = Pad [width=1.7916372540489107 height=0.98511085576570412 connect=center]  # not connected
  Pad89 = Pad [width=1.7916372540489107 height=0.98511085576570412 connect=center]  # not connected
  Pad90 = Pad [width=1.7916372540489107 height=0.98511085576570412 connect=center]  # not connected
  Pad91 = Pad [width=1.7916372540489107 height=0.98511085576570412 connect=center]  # not connected
  Pad92 = Pad [width=1.7916372540489107 height=0.98511085576570412 connect=center]  # not connected
  Pad93 = Pad [width=1.7916372540489107 height=0.98511085576570412 connect=center]  # not connected
  Pad94 = Pad [width=1.7916372540489107 height=0.98511085576570412 connect=center]  # not connected
  Pad95 = Pad [width=1.7916372540489107 height=0.98511085576570412 connect=center]  # not connected
  Pad96 = Pad [width=1.7916372540489107 height=0.98511085576570412 connect=center]  # not connected
  Pad97 = Pad [width=1.7916372540489107 height=0.98511085576570412 connect=center]  # not connected
  Pad98 = Pad [width=1.7916372540489107 height=0.98511085576570412 connect=center]  # not connected
  Pad99 = Pad [width=1.7916372540489107 height=0.98511085576570412 connect=center]  # not connected
  Pad100 = Pad [width=1.7916372540489107 height=0.98511085576570412 connect=center]  # not connected
  Pad101 = Pad [width=1.7916372540489107 height=0.98511085576570412 connect=center]  # not connected
  Pad102 = Pad [width=1.7916372540489107 height=0.98511085576570412 connect=center]  # not connected
  Pad103 = Pad [width=1.7916372540489107 height=0.98511085576570412 connect=center]  # not connected
  Pad104 = Pad [width=1.7916372540489107 height=0.98511085576570412 connect=center]  # not connected
  Pad105 = Pad [width=1.7916372540489107 height=0.98511085576570412 connect=center]  # not connected
  Pad106 = Pad [width=1.7916372540489107 height=0.98511085576570412 connect=center]  # not connected
  Pad107 = Pad [width=1.7916372540489107 height=0.98511085576570412 connect=center]  # not connected
  Pad108 = Pad [width=1.7916372540489107 height=0.98511085576570412 connect=center]  # not connected
  Pad109 = Pad [width=1.7916372540489107 height=0.98511085576570412 connect=center]  # not connected
  Pad110 = Pad [width=1.7916372540489107 height=0.98511085576570412 connect=center]  # not connected
  Pad111 = Pad [width=1.7916372540489107 height=0.98511085576570412 connect=center]  # not connected
  Pad112 = Pad [width=1.7916372540489107 height=0.98511085576570412 connect=center]  # not connected
  Pad113 = Pad [width=1.7916372540489107 height=0.98511085576570412 connect=center]  # not connected
  Pad114 = Pad [width=1.7916372540489107 height=0.98511085576570412 connect=center]  # not connected
  Pad115 = Pad [width=1.7916372540489107 height=0.98511085576570412 connect=center]  # not connected
  Pad116 = Pad [width=1.7916372540489107 height=0.98511085576570412 connect=center]  # not connected
  Pad117 = Pad [width=1.7916372540489107 height=0.98511085576570412 connect=center]  # not connected
  Pad118 = Pad [width=1.7916372540489107 height=0.98511085576570412 connect=center]  # not connected
  Pad119 = Pad [width=1.7916372540489107 height=0.98511085576570412 connect=center]  # not connected
  Pad120 = Pad [width=1.7916372540489107 height=0.98511085576570412 connect=center]  # not connected
  Pad121 = Pad [width=1.7916372540489107 height=0.98511085576570412 connect=center]  # not connected
  Pad122 = Pad [width=2 height=1.5 connect=center]  # not connected
  Pad123 = Pad [width=3.5 height=1.5 connect=center]  # not connected
  Pad124 = Pad [width=4 height=1.5 connect=center]  # not connected
  Pad125 = Pad [width=3.5 height=1.5 connect=center]  # not connected
  Pad126 = Pad [width=2 height=1.5 connect=center]  # not connected
  Pad127 = Pad [width=3.5 height=1.5 connect=center]  # not connected
  Pad128 = Pad [width=2 height=1.5 connect=center]  # not connected
  Pad129 = Pad [width=3.5 height=1.5 connect=center]  # not connected
  Pad130 = Pad [width=4 height=1.5 connect=center]  # not connected
  Pad131 = Pad [width=3.5 height=1.5 connect=center]  # not connected
  Pad132 = Pad [width=4 height=1.5 connect=center]  # not connected
  Pad133 = Pad [width=3.5 height=1.5 connect=center]  # not connected
  Pad134 = Pad [width=4 height=1.5 connect=center]  # not connected
  Pad135 = Pad [width=3.5 height=1.5 connect=center]  # not connected

nets:
  N1: A13.pad, Pad11.pad
  N2: G_3.pad, Pad34.pad
  N3: D6.pad, Pad44.pad
  N4: D1.pad, Pad29.pad
  N5: A12.pad, Pad32.pad
  N6: M8-B.pad, Pad9.pad
  N7: A4.pad, Pad40.pad
  N8: CLK.pad, Pad5.pad
  N9: 5V_2.pad, Pad43.pad
  N10: Refr.pad, Pad12.pad
  N11: A0.pad, Pad38.pad
  N12: A15.pad, Pad4.pad
  N13: Rd.pad, Pad1.pad
  N14: D4.pad, Pad25.pad
  N15: M1.pad, Pad7.pad
  N16: GG.pad, Pad6.pad
  N17: CE.pad, Pad2.pad
  N18: A2.pad, Pad31.pad
  N19: G_4.pad, Pad45.pad
  N20: TVR.pad, Pad3.pad
  N21: A6.pad, Pad27.pad
  N22: A9.pad, Pad8.pad

notes:
  2
  1
  44
  45
  -
  34V
  WR
  A7
  A5
  A3
  A1
  D0
  D2
  A10
  D5
  D7
  D3
  Ground
  D1
  A0
  A2
  A4
  A6
  A12
  5V
  GRD
  D4
  D6
  A14
  IOReg
  Reset
  TV
  TVL
  A8
  A11
  MO-7
  A9
  A13
  M8-B
  M1
  Reference
  Clock
  GG
  TVR
  A15
  Read
  Clear
  33
  35
  37
  39
  41
  43
  31
  29
  27
  30
  32
  34
  36
  38
  40
  42
  28
  26
  24
  17
  19
  21
  23
  15
  25
  13
  11
  7
  9
  5
  3
  14
  12
  6
  10
  4
  8
  18
  20
  16
  22
  ████████████
  C1
  C2
  C3
